# Fritzing sketch Mechanical respirator wiring  (saved by Fritzing 0.9.6b)
breadboards: 2

parts:
  Part1 = Arduino Uno (Rev3)
  S1 = Pushbutton [package="[THT]"]
  S2 = Pushbutton [package="[THT]"]
  S3 = Pushbutton [package="[THT]"]
  M1 = Stepper Motor - Unipolar  # not connected
  R1 = Resistor [tolerance=±5% resistance=10k power=0.25 package=THT]
  S4 = Toggle Switch [package=THT]
  R2 = Resistor [tolerance=±5% resistance=10k power=0.25 package=THT]
  R3 = Resistor [tolerance=±5% resistance=10k power=0.25 package=THT]
  R4 = Resistor [tolerance=±5% resistance=10k power=0.25 package=THT]

nets:
  N1: Part1.D4, S2.Pin_1, S2.Pin_2, R2.Pin_1
  N2: Part1.D5_PWM, S1.Pin_1, S1.Pin_2, R3.Pin_1
  N3: Part1.D7, R1.Pin_1, S4.COM
  N4: Part1.RESET, S3.Pin_1, S3.Pin_2, R4.Pin_1
  N5: Part1.5V, S1.Pin_3, S1.Pin_4, S2.Pin_3, S2.Pin_4, S3.Pin_3, S3.Pin_4, S4.L2
  N6: Part1.GND, R1.Pin_0, R2.Pin_0, R3.Pin_0, R4.Pin_0

notes:
  TB6600A Driver (of Stepper Motor)
  CK
  CLK
  EN
  5 V
  24 Volt D.C
